// Logisim project alu.circ as structural Verilog: 3 circuits, main circuit main
module main (
  input  [31:0] X,
  input  [31:0] Y,
  input  [3:0] Switch,
  output Signed_Overflow,
  output Equal,
  output [31:0] Result
);

  wire and_2_out, and_3_out, comparator_1_lt, comparator_2_lt, comparator_3_eq, comparator_4_eq,
       overflowchecker_1_out, overflowcheckerneg_1_out;
  wire [4:0] bit_extender_1_out;
  wire [31:0] and_1_out, bit_extender_2_out, bit_extender_3_out, or_1_out, shifter_1_out, shifter_2_out,
       shifter_3_out, sub, sum;

  Bit_Extender #(.in_width(32), .out_width(5)) bit_extender_1 (.in(X), .out(bit_extender_1_out));
  Shifter #(.width(32)) shifter_1 (.in(Y), .\dist (bit_extender_1_out), .out(shifter_1_out));
  Shifter #(.width(32), .shift("lr")) shifter_2 (.in(Y), .\dist (bit_extender_1_out), .out(shifter_2_out));
  Shifter #(.width(32), .shift("ar")) shifter_3 (.in(Y), .\dist (bit_extender_1_out), .out(shifter_3_out));
  Adder #(.width(32)) adder_1 (.a(X), .b(Y), .out(sum));  // open: cin, cout
  Subtractor #(.width(32)) subtractor_1 (.a(X), .b(Y), .out(sub));  // open: bin, bout
  assign and_1_out = X & Y;  // AND_Gate and_1, 32 bits wide
  assign or_1_out = X | Y;  // OR_Gate or_1, 32 bits wide
  Comparator #(.width(32)) comparator_1 (.a(X), .b(Y), .lt(comparator_1_lt));  // open: gt, eq
  Comparator #(.width(32), .mode("unsigned")) comparator_2 (.a(X), .b(Y), .lt(comparator_2_lt));  // open: gt, eq
  overflowchecker overflowchecker_1 (.X(X), .Y(Y), .Z(sum), .out(overflowchecker_1_out));
  Comparator #(.width(4), .mode("unsigned")) comparator_3 (
    .a(4'b0101), .b(Switch), .eq(comparator_3_eq));  // open: gt, lt
  Comparator #(.width(4), .mode("unsigned")) comparator_4 (
    .a(Switch), .b(4'b0111), .eq(comparator_4_eq));  // open: gt, lt
  overflowcheckerNEG overflowcheckerneg_1 (.X(X), .Y(Y), .Z(sub), .out(overflowcheckerneg_1_out));
  Comparator #(.width(32), .mode("unsigned")) comparator_5 (.a(X), .b(Y), .eq(Equal));  // open: gt, lt
  assign bit_extender_2_out = {{31{1'b0}}, comparator_1_lt};  // Bit_Extender bit_extender_2
  assign bit_extender_3_out = {{31{1'b0}}, comparator_2_lt};  // Bit_Extender bit_extender_3
  and and_2 (and_2_out, overflowchecker_1_out, comparator_3_eq);
  and and_3 (and_3_out, comparator_4_eq, overflowcheckerneg_1_out);
  Multiplexer #(.select(4), .width(32), .enable("false")) multiplexer_1 (
    .in0(shifter_1_out), .in1(shifter_2_out), .in2(shifter_3_out), .in5(sum), .in6(sum), .in7(sub),
    .in8(sub), .in9(and_1_out), .in10(or_1_out), .in11(bit_extender_2_out), .in12(bit_extender_3_out),
    .out(Result), .sel(Switch));  // open: in3, in4, in13, in14, in15
  or or_2 (Signed_Overflow, and_2_out, and_3_out);

  // Other names for the same wires on the sheet: overflow = Signed_Overflow; S[3:0] = Switch

  // Notes on the sheet:
  //   INPUTS to your circuit
  //   DON'T CHANGE THE LOCATIONS OF THE INPUTS AND OUTPUTS!
  //   OUTPUTS from your circuit
endmodule

module overflowchecker (
  input  [31:0] X,
  input  [31:0] Y,
  input  [31:0] Z,
  output out
);

  wire and_1_out, and_2_out;

  and and_1 (and_1_out, X[31], Y[31], ~Z[31]);  // AND_Gate
  and and_2 (and_2_out, ~X[31], ~Y[31], Z[31]);  // AND_Gate
  or or_1 (out, and_1_out, and_2_out);
endmodule

module overflowcheckerNEG (
  input  [31:0] X,
  input  [31:0] Y,
  input  [31:0] Z,
  output out
);

  wire not_1_out, xor_1_out, xor_2_out;

  xor xor_1 (xor_1_out, X[31], Y[31]);
  xor xor_2 (xor_2_out, Y[31], Z[31]);
  not not_1 (not_1_out, xor_2_out);
  and and_1 (out, xor_1_out, not_1_out);
endmodule
