// Logisim project cpu.circ as structural Verilog: 2 circuits, main circuit main
module main (
  input  [31:0] INSTRUCTION,
  input  CLOCK,
  output [31:0] FETCH_ADDRESS,
  output [31:0] s0_Value,
  output [31:0] s1_Value,
  output [31:0] s2_Value,
  output [31:0] ra_Value,
  output [31:0] sp_Value
);

  wire ALUSrc, and_1_out, branchCond, eql, ExtOp, jal, lui, main_2_signed_overflow, MemToReg, MemWr, op0,
       or_1_out, RegWr, shift;
  wire [1:0] nPCsel, RegDst;
  wire [3:0] ALUCtr;
  wire [4:0] multiplexer_2_out, multiplexer_4_out, shamt;
  wire [5:0] funct, opcode;
  wire [25:11] register_1_q;
  wire [31:0] adder_2_out, adder_3_out, bit_extender_1_out, bit_extender_2_out, bit_extender_3_out, immed,
       main_2_result, main_3_p5, multiplexer_1_out, multiplexer_3_out, multiplexer_6_out, multiplexer_7_out,
       multiplexer_8_out, multiplexer_9_out, multiplexer_10_out, PC_4, R_rs, register_2_q, rt, shifter_1_out,
       shifter_2_out, shifter_3_out, WrtData;

  and and_1 (and_1_out, nPCsel[0], branchCond);
  or or_1 (or_1_out, nPCsel[1], and_1_out);
  Multiplexer #(.width(32), .enable("false")) multiplexer_1 (
    .in0(INSTRUCTION), .in1({32{1'b0}}), .out(multiplexer_1_out), .sel(or_1_out));
  Register #(.width(32)) register_1 (
    .D(multiplexer_1_out), .Q({opcode, register_1_q, shamt, funct}), .clk(CLOCK));  // open: en, clr
  Adder #(.width(32)) adder_1 (.a(FETCH_ADDRESS), .b(32'h4), .out(PC_4));  // open: cin, cout
  Shifter #(.width(32)) shifter_1 (.in(immed), .\dist (5'b00010), .out(shifter_1_out));
  Shifter #(.width(32)) shifter_2 (.in({opcode, register_1_q, shamt, funct}), .\dist (5'b00010), .out(shifter_2_out));
  Multiplexer #(.select(2), .width(5), .enable("false")) multiplexer_2 (
    .in0(register_1_q[20:16]), .in1(register_1_q[15:11]), .in2(register_1_q[25:21]), .out(multiplexer_2_out),
    .sel(RegDst));  // open: in3
  Multiplexer #(.width(32), .enable("false")) multiplexer_3 (
    .in0(PC_4), .in1(adder_2_out), .out(multiplexer_3_out), .sel(branchCond));
  Adder #(.width(32)) adder_2 (.a(adder_3_out), .b(shifter_1_out), .out(adder_2_out));  // open: cin, cout
  xor xor_1 (branchCond, eql, op0);
  assign bit_extender_1_out = {{16{1'b0}}, {register_1_q[15:11], shamt, funct}};  // Bit_Extender bit_extender_1
  assign bit_extender_2_out = {{16{register_1_q[15]}}, {register_1_q[15:11], shamt, funct}};  // Bit_Extender bit_extender_2
  Multiplexer #(.width(5), .enable("false")) multiplexer_4 (
    .in0(multiplexer_2_out), .in1({5{1'b1}}), .out(multiplexer_4_out), .sel(jal));
  Multiplexer #(.width(32), .enable("false")) multiplexer_5 (
    .in0(bit_extender_1_out), .in1(bit_extender_2_out), .out(immed), .sel(ExtOp));
  Multiplexer #(.select(2), .width(32), .enable("false")) multiplexer_6 (
    .in0(PC_4), .in1(multiplexer_3_out), .in2({adder_3_out[31:28], shifter_2_out[27:0]}), .in3(R_rs),
    .out(multiplexer_6_out), .sel(nPCsel));
  Register #(.width(32)) PC (.D(multiplexer_6_out), .Q(FETCH_ADDRESS), .clk(CLOCK));  // open: en, clr
  regfile_main main_1 (
    .Read_Register_1(register_1_q[25:21]), .Read_Register_2(register_1_q[20:16]),
    .Write_Register(multiplexer_4_out), .Write_Data(WrtData), .Write_Enable(RegWr), .Clock(CLOCK),
    .Read_Data_1(R_rs), .Read_Data_2(rt), .s0_Value(s0_Value), .s1_Value(s1_Value), .s2_Value(s2_Value),
    .ra_Value(ra_Value), .sp_Value(sp_Value));
  Multiplexer #(.width(32), .enable("false")) multiplexer_7 (
    .in0(rt), .in1(immed), .out(multiplexer_7_out), .sel(ALUSrc));
  Register #(.width(32)) register_2 (.D(FETCH_ADDRESS), .Q(register_2_q), .clk(CLOCK));  // open: en, clr
  Adder #(.width(32)) adder_3 (.a(register_2_q), .b(32'h4), .out(adder_3_out));  // open: cin, cout
  Multiplexer #(.width(32), .enable("false")) multiplexer_8 (
    .in0(R_rs), .in1(bit_extender_3_out), .out(multiplexer_8_out), .sel(shift));
  assign bit_extender_3_out = {{27{1'b0}}, shamt};  // Bit_Extender bit_extender_3
  LED led_1 (.in(main_2_signed_overflow));
  alu_main main_2 (
    .Switch(ALUCtr), .X(multiplexer_8_out), .Equal(eql), .Result(main_2_result),
    .Signed_Overflow(main_2_signed_overflow), .Y(multiplexer_7_out));
  Multiplexer #(.width(32), .enable("false")) multiplexer_9 (
    .in0(main_2_result), .in1(shifter_3_out), .out(multiplexer_9_out), .sel(lui));
  Shifter #(.width(32)) shifter_3 (.in(immed), .\dist (5'b10000), .out(shifter_3_out));
  ctrSignals ctrsignals_1 (
    .opcode(opcode), .ExtOp(ExtOp), .lui(lui), .jal(jal), .shift(shift), .ALUSrc(ALUSrc), .RegWr(RegWr),
    .RegDst(RegDst), .MemToReg(MemToReg), .MemWr(MemWr), .nPCsel(nPCsel), .op0(op0), .funct(funct),
    .AluCtr(ALUCtr));
  // mem_main main_3: pin names not known; wires that end beside it: multiplexer_9_out, rt, MemWr, CLOCK, main_3_p5
  Multiplexer #(.width(32), .enable("false")) multiplexer_10 (
    .in0(multiplexer_9_out), .in1(main_3_p5), .out(multiplexer_10_out), .sel(MemToReg));
  Multiplexer #(.width(32), .enable("false")) multiplexer_11 (
    .in0(multiplexer_10_out), .in1(FETCH_ADDRESS), .out(WrtData), .sel(jal));

  // Other names for the same wires on the sheet: clk = CLOCK; fetch_addr[31:0] = FETCH_ADDRESS; ra[31:0] = ra_Value;
  //   s0[31:0] = s0_Value; s1[31:0] = s1_Value; s2[31:0] = s2_Value; sp[31:0] = sp_Value

  // Notes on the sheet:
  //   Output
  //   These are outputs/inputs from run.circ
  //   Inputs
  //   These are DEBUG/TEST outputs from your circuit.
endmodule

module ctrSignals (
  input  [5:0] opcode,
  input  [5:0] funct,
  output op0,
  output ALUSrc,
  output RegWr,
  output [1:0] RegDst,
  output MemToReg,
  output MemWr,
  output [1:0] nPCsel,
  output [3:0] AluCtr,
  output ExtOp,
  output lui,
  output jal,
  output shift
);

  wire add, addi, addiu, addu, \and , andi, beq, bne, j, jr, \or , or_6_out, ori, rtype, sll, slt, slti,
       sltiu, sltu, sra, srl, sub, subu, sw;

  and and_1 (rtype, ~opcode[0], ~opcode[1], ~opcode[2], ~opcode[3], ~opcode[4], ~opcode[5]);  // AND_Gate
  and and_2 (add, ~funct[0], ~funct[1], ~funct[2], ~funct[3], ~funct[4], funct[5], rtype);  // AND_Gate
  and and_3 (addu, funct[0], ~funct[1], ~funct[2], ~funct[3], ~funct[4], funct[5], rtype);  // AND_Gate
  and and_4 (\and , ~funct[0], ~funct[1], funct[2], ~funct[3], ~funct[4], funct[5], rtype);  // AND_Gate
  and and_5 (jr, ~funct[0], ~funct[1], ~funct[2], funct[3], ~funct[4], ~funct[5], rtype);  // AND_Gate
  or or_1 (AluCtr[3], subu, sltu, sltiu, slti, \and , andi, \or , ori, slt);
  and and_6 (\or , funct[0], ~funct[1], funct[2], ~funct[3], ~funct[4], funct[5], rtype);  // AND_Gate
  and and_7 (slt, ~funct[0], funct[1], ~funct[2], funct[3], ~funct[4], funct[5], rtype);  // AND_Gate
  and and_8 (sltu, funct[0], funct[1], ~funct[2], funct[3], ~funct[4], funct[5], rtype);  // AND_Gate
  and and_9 (sll, ~funct[0], ~funct[1], ~funct[2], ~funct[3], ~funct[4], ~funct[5], rtype);  // AND_Gate
  or or_2 (AluCtr[2], sub, RegDst[1], sw, sltu, sltiu, add, addi, addiu, addu, MemToReg);
  and and_10 (sra, funct[0], ~funct[1], ~funct[2], funct[3], funct[4], ~funct[5], rtype);  // AND_Gate
  and and_11 (srl, ~funct[0], funct[1], ~funct[2], ~funct[3], ~funct[4], ~funct[5], rtype);  // AND_Gate
  and and_12 (sub, ~funct[0], funct[1], ~funct[2], ~funct[3], ~funct[4], funct[5], rtype);  // AND_Gate
  and and_13 (subu, funct[0], funct[1], ~funct[2], ~funct[3], ~funct[4], funct[5], rtype);  // AND_Gate
  or or_3 (AluCtr[1], sub, sra, slti, addiu, addu, \or , ori, slt);
  and and_14 (addi, ~opcode[0], ~opcode[1], ~opcode[2], opcode[3], ~opcode[4], ~opcode[5]);  // AND_Gate
  and and_15 (addiu, opcode[0], ~opcode[1], ~opcode[2], opcode[3], ~opcode[4], ~opcode[5]);  // AND_Gate
  and and_16 (andi, ~opcode[0], ~opcode[1], opcode[2], opcode[3], ~opcode[4], ~opcode[5]);  // AND_Gate
  and and_17 (beq, ~opcode[0], ~opcode[1], opcode[2], ~opcode[3], ~opcode[4], ~opcode[5]);  // AND_Gate
  or or_4 (AluCtr[0], sub, RegDst[1], sw, srl, slti, add, addi, \and , andi, MemToReg, slt);
  and and_18 (bne, opcode[0], ~opcode[1], opcode[2], ~opcode[3], ~opcode[4], ~opcode[5]);  // AND_Gate
  and and_19 (j, ~opcode[0], opcode[1], ~opcode[2], ~opcode[3], ~opcode[4], ~opcode[5]);  // AND_Gate
  and and_20 (jal, opcode[0], opcode[1], ~opcode[2], ~opcode[3], ~opcode[4], ~opcode[5]);  // AND_Gate
  and and_21 (lui, opcode[0], opcode[1], opcode[2], opcode[3], ~opcode[4], ~opcode[5]);  // AND_Gate
  and and_22 (MemToReg, opcode[0], opcode[1], ~opcode[2], ~opcode[3], ~opcode[4], opcode[5]);  // AND_Gate
  and and_23 (ori, opcode[0], ~opcode[1], opcode[2], opcode[3], ~opcode[4], ~opcode[5]);  // AND_Gate
  and and_24 (slti, ~opcode[0], opcode[1], ~opcode[2], opcode[3], ~opcode[4], ~opcode[5]);  // AND_Gate
  and and_25 (sltiu, opcode[0], opcode[1], ~opcode[2], opcode[3], ~opcode[4], ~opcode[5]);  // AND_Gate
  and and_26 (sw, opcode[0], opcode[1], ~opcode[2], opcode[3], ~opcode[4], opcode[5]);  // AND_Gate
  and and_27 (RegDst[1], ~opcode[0], ~opcode[1], opcode[2], opcode[3], ~opcode[4], opcode[5]);  // AND_Gate
  or or_5 (ALUSrc, RegDst[1], sw, sltiu, slti, ori, addi, addiu, andi, MemToReg);
  or or_6 (or_6_out, sw, beq, bne, j, jr);
  not not_1 (RegWr, or_6_out);
  or or_7 (RegDst[0], subu, sub, srl, sra, sll, sltu, slt, \or , add, addu, \and );
  or or_8 (shift, sll, srl, sra);
  or or_9 (ExtOp, addi, RegDst[1], MemToReg, addiu, slti, sw, beq, sltiu, bne);
  or or_10 (MemWr, RegDst[1], sw);
  or or_11 (nPCsel[1], jal, j, jr);
  or or_12 (nPCsel[0], jr, beq, bne);

  assign op0 = opcode[0];

  // Other names for the same wires on the sheet: AluCtr_0 = AluCtr[0]; AluCtr_1 = AluCtr[1]; AluCtr_2 = AluCtr[2];
  //   AluCtr_3 = AluCtr[3]; fn0 = funct[0]; fn1 = funct[1]; fn2 = funct[2]; fn3 = funct[3]; fn4 = funct[4];
  //   fn5 = funct[5]; lw = MemToReg; op1 = opcode[1]; op2 = opcode[2]; op3 = opcode[3]; op4 = opcode[4];
  //   op5 = opcode[5]; swinc = RegDst[1]
endmodule
